# Fritzing sketch lcd_to_rpi (saved by Fritzing 0.9.3b)
breadboards: 1

parts:
  U1 = LCD-16X2 [package=lcd-16x2]
  Raspberry_Pi_1 = Raspberry Pi 3 [part_number=RPI-3-V1.2]
  U2 = POT_SWITCH [package=pot_pth]
  Part1 = Arduino Micro (Rev3)
  S1 = Pushbutton [package="[SMD]"]
  S2 = Pushbutton [package="[SMD]"]
  S3 = Pushbutton [package="[SMD]"]
  S4 = Pushbutton [package="[SMD]"]

nets:
  VSS: U1.VSS, Part1.D2/SDA, Part1.D3/SCL, Part1.D4_PWM/A6, Part1.D5_PWM, Part1.GND, S1.Pin_1, S1.Pin_2, S2.Pin_1, S2.Pin_2, S3.Pin_1, S3.Pin_2, S4.Pin_1, S4.Pin_2
  VDD: U1.VDD, Part1.5V, S1.Pin_3, S1.Pin_4, S2.Pin_3, S2.Pin_4, S3.Pin_3, S3.Pin_4, S4.Pin_3, S4.Pin_4
  N1: U1.VO, U2.G$2_1
  N2: U1.RS, Raspberry_Pi_1.GPIO26
  N3: U1.R_W, U1.E, Raspberry_Pi_1.GPIO19
  N4: U1.DB3, U1.DB4, Raspberry_Pi_1.GPIO13
  N5: U1.DB5, Raspberry_Pi_1.GPIO6
  N6: U1.DB6, Raspberry_Pi_1.GPIO5
  N7: U1.DB7, Raspberry_Pi_1.GPIO11
  N8: U1.A, Raspberry_Pi_1.3v3
  N9: U1.K, Raspberry_Pi_1.GND
